# Fritzing sketch montage_blink (saved by Fritzing 0.9.6b)
breadboards: 1

parts:
  LED1 = LED - 5mm [color="Red (633nm)" current=0.030 package="5 mm [THT]"]
  R1 = Resistor [tolerance=±5% power=0.25 resistance=220 package=THT]
  Composant1 = Arduino Uno (Rev3)

nets:
  N1: LED1.cathode, Composant1.GND
  N2: LED1.anode, R1.Pin_0
  N3: R1.Pin_1, Composant1.D13/SCK

// code stored in the sketch: montage_blink.ino
/*
  Clignotement
  Allume la LED 13 pendant 1 seconde,
  puis l'éteint pendant 1 seconde.
*/

// On stocke la valeur 13 dans la variable "led", pour indiquer que la led se trouve sur la broche 13 
// La variable "led" est un nombre entier (integer in english)
int led = 13;

// le code dans cette fonction est exécuté une fois au début 
void setup() {

// indique que la broche de la LED 13 est une sortie :  
pinMode(led, OUTPUT); 
} 

// le code dans cette fonction est exécuté en boucle 
void loop() {  
digitalWrite(led, HIGH);   // allumer la LED (tension 5V sur la broche)  
delay(1000);                       // attendre 1000ms = 1s  
digitalWrite(led, LOW);    // éteindre la LED (tension 0V sur la broche)  
delay(1000);                       // attendre à nouveau 1 seconde 
}
