# Fritzing sketch prototypage et electricité (saved by Fritzing 0.9.6b)
breadboards: 1

parts:
  LED1 = smd LED [color="Red (633nm)" package="0805 [SMD]"]
  R1 = Resistor [tolerance=±5% power=0.25 resistance=220 package=THT]
  S1 = Toggle Switch [package=THT]
  VCC1 = Battery

nets:
  N1: LED1.cathode, VCC1.+
  N2: LED1.anode, R1.Pin_0
  N3: R1.Pin_1, S1.L1
  N4: S1.COM, VCC1.-
